# Fritzing sketch PCB_Photon (saved by Fritzing 0.9.3b)
circuit board: 3.66607cm x 2.05174cm

parts:
  R1 = Resistor [tolerance=±5% resistance=220 package="0805 [SMD]"]
  LED2 = LED - 3mm [color="Red (633nm)" package="3 mm [THT]"]
  LED3 = LED - 3mm [color="Red (633nm)" package="3 mm [THT]"]
  R2 = Resistor [tolerance=±5% resistance=220 package="0805 [SMD]"]
  220ohm_R = Resistor [tolerance=±5% resistance=220 package="0805 [SMD]"]
  LED1 = LED - 3mm [color="Red (633nm)" package="3 mm [THT]"]

nets:
  N1: R1.Pin_0, LED1.anode
  N2: R1.Pin_1, R2.Pin_1, 220ohm_R.Pin_1
  N3: LED2.anode, 220ohm_R.Pin_0
  N4: LED3.anode, R2.Pin_0
