# Fritzing sketch PCB_Pi (saved by Fritzing 0.9.3b)
circuit board: 8.54428cm x 5.64269cm

parts:
  Yellow_Button = Pushbutton [package="[THT]"]
  Blue_Button = Pushbutton [package="[THT]"]
  Red_Button = Pushbutton [package="[THT]"]
  Green_Button = Pushbutton [package="[THT]"]
  220ohm_R = Resistor [tolerance=±5% resistance=220 package="0805 [SMD]"]
  Pi_40-pin_Header = Raspberry Pi Header 40pin [form="♂ (male)" package=THT]
  220ohm_R_2 = Resistor [tolerance=±5% resistance=220 package="0805 [SMD]"]
  220ohm_R_3 = Resistor [tolerance=±5% resistance=220 package="0805 [SMD]"]
  220ohm_R_4 = Resistor [tolerance=±5% resistance=220 package="0805 [SMD]"]

nets:
  N1: Yellow_Button.Pin_1, Yellow_Button.Pin_2, 220ohm_R.Pin_0, Pi_40-pin_Header.GIPO27
  N2: Yellow_Button.Pin_4, Blue_Button.Pin_4, Red_Button.Pin_4, Green_Button.Pin_3, Green_Button.Pin_4, Pi_40-pin_Header.GND
  N3: Blue_Button.Pin_1, Blue_Button.Pin_2, Pi_40-pin_Header.GIPO4, 220ohm_R_2.Pin_0
  N4: Red_Button.Pin_1, Red_Button.Pin_2, Pi_40-pin_Header.GIPO22, 220ohm_R_3.Pin_0
  N5: Green_Button.Pin_1, Green_Button.Pin_2, Pi_40-pin_Header.GIPO19, 220ohm_R_4.Pin_0
  3V3: 220ohm_R.Pin_1, Pi_40-pin_Header.3v3, Pi_40-pin_Header.3V3, 220ohm_R_2.Pin_1, 220ohm_R_3.Pin_1, 220ohm_R_4.Pin_1

custom parts:
  Raspberry Pi Header 40pin: Raspberry Pi 40 pin header - for creating your own shields.
